# Fritzing sketch Fortune_Teller_4a (saved by Fritzing 1.0.6)
circuit board: 14.1cm x 6.2cm
breadboards: 3

parts:
  Coin_Drop_Switch = Momentary Switch [package=ksa_sealed_tac_switch]
  3_3_v_Regulator = female pin header, 3 pins [form="♀ (female)"]
  DAC/Amp = female pin header, 7 pins [form="♀ (female)"]
  VCC = female pin header, 2 pins [form="♀ (female)"]
  Round_Display = GC9A01 round lcd
  C1 = Capacitor [package=cap-pth-small]
  A1 = ESP32-S3-WROOM-1-N16R8 dev board
  Header = female pin header, 12 pins [form="♀ (female)"]
  header = female pin header, 7 pins [form="♀ (female)"]
  J1 = female pin header, 2 pins [form="♀ (female)"]
  J2 = female pin header, 2 pins [form="♀ (female)"]
  J3 = female pin header, 3 pins [form="♀ (female)"]
  J4 = female pin header, 3 pins [form="♀ (female)"]
  J5 = female pin header, 3 pins [form="♀ (female)"]

nets:
  N1: Coin_Drop_Switch.1, Coin_Drop_Switch.2, 3_3_v_Regulator.pin3, DAC/Amp.pin2, DAC/Amp.pin4, VCC.pin2, Round_Display.Pin_6, C1.2, A1.Pin_22, A1.Pin_23, A1.Pin_24, A1.Pin_44, J1.pin1, J1.pin2, J3.pin1
  N2: Coin_Drop_Switch.3, Coin_Drop_Switch.4, A1.Pin_25
  N3: 3_3_v_Regulator.pin1, VCC.pin1, A1.Pin_21, J3.pin2
  N4: 3_3_v_Regulator.pin2, DAC/Amp.pin1
  N5: DAC/Amp.pin5, A1.Pin_27
  N6: DAC/Amp.pin6, A1.Pin_26
  N7: DAC/Amp.pin7, A1.Pin_6, J4.pin2
  N8: Round_Display.Pin_1, A1.Pin_4
  N9: Round_Display.Pin_2, A1.Pin_8
  N10: Round_Display.Pin_3, A1.Pin_40
  N11: Round_Display.Pin_4, A1.Pin_19
  N12: Round_Display.Pin_5, A1.Pin_11
  N13: Round_Display.Pin_7, C1.1, A1.Pin_1, A1.Pin_2
  N14: A1.Pin_5, J4.pin3
  N15: A1.Pin_7, J4.pin1
  N16: A1.Pin_9, J2.pin2
  N17: A1.Pin_10, J2.pin1
  N18: A1.Pin_12, header.pin7
  N19: A1.Pin_13, header.pin6
  N20: A1.Pin_14, header.pin5
  N21: A1.Pin_15, header.pin4
  N22: A1.Pin_16, header.pin3
  N23: A1.Pin_17, header.pin2
  N24: A1.Pin_18, header.pin1
  N25: A1.Pin_20, J3.pin3
  N26: A1.Pin_28, Header.pin1
  N27: A1.Pin_29, Header.pin2
  N28: A1.Pin_30, Header.pin3
  N29: A1.Pin_31, Header.pin4
  N30: A1.Pin_32, Header.pin5
  N31: A1.Pin_33, Header.pin6
  N32: A1.Pin_34, Header.pin7
  N33: A1.Pin_35, Header.pin8
  N34: A1.Pin_36, Header.pin9
  N35: A1.Pin_37, Header.pin10
  N36: A1.Pin_38, Header.pin11
  N37: A1.Pin_39, Header.pin12
  N38: A1.Pin_41, J5.pin1
  N39: A1.Pin_42, J5.pin2
  N40: A1.Pin_43, J5.pin3

custom parts:
  GC9A01 round lcd: IPS TFT display round 1.28″ 240×240 GC9A01 controller. Mar 2025 fix pcb pin with fill #ffffff instead of none. Casuses problem in etchable pcb images (pad with no hole.)
  ESP32-S3-WROOM-1-N16R8 dev board: ESP32-S3 WIFI+BLE5.0 Development Board ESP32-S3-WROOM-1-N16R8(16M Flash/8SRAM).
